# Fritzing sketch Schematic (saved by Fritzing 0.9.6b)
breadboards: 1

parts:
  Part1 = Arduino Uno (Rev3)
  Part2 = OLED Monochrome 128x64 1.3 inch [part_number=SSD1306]
  Up = Pushbutton [package="[THT]"]
  Down = Pushbutton [package="[THT]"]
  Left = Pushbutton [package="[THT]"]
  Right = Pushbutton [package="[THT]"]

nets:
  N1: Part1.A4/SDA, Part2.MOSI_SDA
  N2: Part1.A5/SCL, Part2.SCLK_SCK
  GND: Part1.GND, Part2.GND, Up.Pin_1, Up.Pin_2, Down.Pin_1, Down.Pin_2, Left.Pin_2, Right.Pin_2
  N3: Part1.D2, Up.Pin_3, Up.Pin_4
  N4: Part1.D3_PWM, Left.Pin_3, Left.Pin_4
  N5: Part1.D4, Down.Pin_3, Down.Pin_4
  N6: Part1.D5_PWM, Right.Pin_3, Right.Pin_4
  3V3: Part1.3V3, Part2.VIN

custom parts:
  OLED Monochrome 128x64 1.3 inch: These displays are small, only about 1.3" diagonal, but very readable due to the high contrast of an OLED display. This display is made of 128x64 individual white OLED pixels, each one is turned on or off by the controller chip. Because the display makes its own light, no backlight is required. This reduces the power required to run the OLED and is why the display has such high contrast; we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
